// Logisim project RF16_32b_DualPort.circ as structural Verilog: 1 circuit, main circuit main
module main (
  input  [3:0] AD1,
  input  [3:0] AD2,
  input  CLK,
  input  WE,
  input  [3:0] AD3,
  input  [31:0] WD3,
  output [31:0] RD1,
  output [31:0] RD2
);

  wire [31:0] demultiplexer_1_out0, demultiplexer_1_out1, demultiplexer_1_out2, demultiplexer_1_out3,
       main_1_rd1, main_1_rd2, main_2_rd1, main_2_rd2, main_3_rd1, main_3_rd2, main_4_rd1, main_4_rd2;

  Demultiplexer #(.select(2), .width(32)) demultiplexer_1 (
    .out0(demultiplexer_1_out0), .out1(demultiplexer_1_out1), .out2(demultiplexer_1_out2),
    .out3(demultiplexer_1_out3), .in(WD3), .sel(AD3[3:2]));  // open: en
  RF4_32b_DualPort_main main_1 (
    .CLOCK(CLK), .WD(demultiplexer_1_out0), .AD1(AD1[1:0]), .AD3(AD3[1:0]), .WE(WE), .AD2(AD2[1:0]),
    .RD1(main_1_rd1), .RD2(main_1_rd2));
  RF4_32b_DualPort_main main_2 (
    .CLOCK(CLK), .WD(demultiplexer_1_out1), .AD1(AD1[1:0]), .AD3(AD3[1:0]), .WE(WE), .AD2(AD2[1:0]),
    .RD1(main_2_rd1), .RD2(main_2_rd2));
  RF4_32b_DualPort_main main_3 (
    .CLOCK(CLK), .WD(demultiplexer_1_out2), .AD1(AD1[1:0]), .AD3(AD3[1:0]), .WE(WE), .AD2(AD2[1:0]),
    .RD1(main_3_rd1), .RD2(main_3_rd2));
  RF4_32b_DualPort_main main_4 (
    .CLOCK(CLK), .WD(demultiplexer_1_out3), .AD1(AD1[1:0]), .AD3(AD3[1:0]), .WE(WE), .AD2(AD2[1:0]),
    .RD1(main_4_rd1), .RD2(main_4_rd2));
  Multiplexer #(.select(2), .width(32)) multiplexer_1 (
    .in0(main_1_rd1), .in1(main_2_rd1), .in2(main_3_rd1), .in3(main_4_rd1), .out(RD1), .sel(AD1[3:2]));  // open: en
  Multiplexer #(.select(2), .width(32)) multiplexer_2 (
    .in0(main_1_rd2), .in1(main_2_rd2), .in2(main_3_rd2), .in3(main_4_rd2), .out(RD2), .sel(AD2[3:2]));  // open: en
endmodule
