// Logisim project RegFile.circ as structural Verilog: 1 circuit, main circuit main
module main (
  input  [4:0] A1,
  input  [4:0] A2,
  input  in_3,
  input  [4:0] A3,
  input  [31:0] WD3,
  input  in_6,
  output [31:0] RD1,
  output [31:0] RD2
);

  wire demultiplexer_2_out0, demultiplexer_2_out1;
  wire [31:0] demultiplexer_1_out0, demultiplexer_1_out1, main_1_rd1, main_1_rd2, main_2_rd1, main_2_rd2;

  Demultiplexer #(.width(32)) demultiplexer_1 (
    .out0(demultiplexer_1_out0), .out1(demultiplexer_1_out1), .in(WD3), .sel(A3[4]));  // open: en
  Demultiplexer demultiplexer_2 (
    .out0(demultiplexer_2_out0), .out1(demultiplexer_2_out1), .in(in_6), .sel(A3[4]));  // open: en
  regfile16_main main_1 (
    .A1(A1[3:0]), .A2(A2[3:0]), .CLK(in_3), .WE(demultiplexer_2_out0), .A3(A3[3:0]),
    .WD3(demultiplexer_1_out0), .RD1(main_1_rd1), .RD2(main_1_rd2));
  regfile16_main main_2 (
    .A1(A1[3:0]), .A2(A2[3:0]), .CLK(in_3), .WE(demultiplexer_2_out1), .A3(A3[3:0]),
    .WD3(demultiplexer_1_out1), .RD1(main_2_rd1), .RD2(main_2_rd2));
  Multiplexer #(.width(32)) multiplexer_1 (.in0(main_1_rd1), .in1(main_2_rd1), .out(RD1), .sel(A1[4]));  // open: en
  Multiplexer #(.width(32)) multiplexer_2 (.in0(main_1_rd2), .in1(main_2_rd2), .out(RD2), .sel(A2[4]));  // open: en
endmodule
