// Logisim project RegFile32.circ as structural Verilog: 1 circuit, main circuit main
module main (
  input  CLK,
  input  WE,
  input  [4:0] AD1,
  input  [4:0] AD2,
  input  [4:0] AD3,
  input  [31:0] in_6,
  output [31:0] out_7,
  output [31:0] out_8
);

  wire [31:0] demultiplexer_1_out0, demultiplexer_1_out1, main_1_rd1, main_1_rd2, main_2_rd1, main_2_rd2;

  Demultiplexer #(.width(32)) demultiplexer_1 (
    .out0(demultiplexer_1_out0), .out1(demultiplexer_1_out1), .in(in_6), .sel(AD3[4]));  // open: en
  RF16_32b_DualPort_main main_1 (
    .AD1(AD1[3:0]), .AD2(AD2[3:0]), .CLK(CLK), .AD3(AD3[3:0]), .WD3(demultiplexer_1_out0), .WE(WE),
    .RD1(main_1_rd1), .RD2(main_1_rd2));
  RF16_32b_DualPort_main main_2 (
    .AD1(AD1[3:0]), .AD2(AD2[3:0]), .CLK(CLK), .AD3(AD3[3:0]), .WD3(demultiplexer_1_out1), .WE(WE),
    .RD1(main_2_rd1), .RD2(main_2_rd2));
  Multiplexer #(.width(32)) multiplexer_1 (.in0(main_1_rd1), .in1(main_2_rd1), .out(out_7), .sel(AD1[4]));  // open: en
  Multiplexer #(.width(32)) multiplexer_2 (.in0(main_1_rd2), .in1(main_2_rd2), .out(out_8), .sel(AD2[4]));  // open: en
endmodule
