// Logisim project alu32.circ as structural Verilog: 1 circuit, main circuit main
module main (
  input  [31:0] A,
  input  [31:0] B,
  input  [2:0] F,
  output [31:0] Y,
  output Zero
);

  wire [30:0] adder_1_out;
  wire [31:0] and_1_out, bit_extender_1_out, multiplexer_1_out, not_1_out, or_1_out;
  wire [31:31] adder_1_out_2;

  assign not_1_out = ~B;  // NOT_Gate not_1, 32 bits wide
  Multiplexer #(.width(32)) multiplexer_1 (.in0(B), .in1(not_1_out), .out(multiplexer_1_out), .sel(F[2]));  // open: en
  assign and_1_out = A & multiplexer_1_out;  // AND_Gate and_1, 32 bits wide
  assign or_1_out = A | multiplexer_1_out;  // OR_Gate or_1, 32 bits wide
  Adder #(.width(32)) adder_1 (
    .a(A), .b(multiplexer_1_out), .out({adder_1_out_2[31], adder_1_out}), .cin(F[2]));  // open: cout
  assign bit_extender_1_out = {{31{1'b0}}, adder_1_out_2[31]};  // Bit_Extender bit_extender_1
  Multiplexer #(.select(2), .width(32)) multiplexer_2 (
    .in0(and_1_out), .in1(or_1_out), .in2({adder_1_out_2[31], adder_1_out}), .in3(bit_extender_1_out),
    .out(Y), .sel(F[1:0]));  // open: en
  nor nor_1 (Zero, adder_1_out[0], adder_1_out[1], adder_1_out[2], adder_1_out[3], adder_1_out[4], adder_1_out[5], adder_1_out[6], adder_1_out[7], adder_1_out[8], adder_1_out[9], adder_1_out[10], adder_1_out[11], adder_1_out[12], adder_1_out[13], adder_1_out[14], adder_1_out[15], adder_1_out[16], adder_1_out[17], adder_1_out[18], adder_1_out[19], adder_1_out[20], adder_1_out[21], adder_1_out[22], adder_1_out[23], adder_1_out[24], adder_1_out[25], adder_1_out[26], adder_1_out[27], adder_1_out[28], adder_1_out[29], adder_1_out[30], adder_1_out_2[31]);

  // Notes on the sheet:
  //   1 if A - B < 0
endmodule
