// Logisim project logisim_Heart_on_LED_Matrix.circ as structural Verilog: 1 circuit, main circuit main
module main (
  input  in_1
);

  wire clock_1_out;
  wire [15:0] multiplexer_1_out, multiplexer_2_out, multiplexer_3_out, multiplexer_4_out, multiplexer_5_out,
       multiplexer_6_out, multiplexer_7_out, multiplexer_8_out, register_1_q, register_2_q, register_3_q,
       register_4_q, register_5_q, register_6_q, register_7_q, register_8_q;

  Clock clock_1 (.out(clock_1_out));
  Multiplexer #(.width(16)) multiplexer_1 (
    .in0(register_8_q), .in1(16'h300), .out(multiplexer_1_out), .sel(in_1));  // open: en
  Register #(.width(16)) register_1 (.D(multiplexer_1_out), .Q(register_1_q), .clk(clock_1_out));  // open: en, clr
  Multiplexer #(.width(16)) multiplexer_2 (
    .in0(register_1_q), .in1(16'h480), .out(multiplexer_2_out), .sel(in_1));  // open: en
  Register #(.width(16)) register_2 (.D(multiplexer_2_out), .Q(register_2_q), .clk(clock_1_out));  // open: en, clr
  Multiplexer #(.width(16)) multiplexer_3 (
    .in0(register_2_q), .in1(16'h840), .out(multiplexer_3_out), .sel(in_1));  // open: en
  Register #(.width(16)) register_3 (.D(multiplexer_3_out), .Q(register_3_q), .clk(clock_1_out));  // open: en, clr
  Multiplexer #(.width(16)) multiplexer_4 (
    .in0(register_3_q), .in1(16'h1020), .out(multiplexer_4_out), .sel(in_1));  // open: en
  Register #(.width(16)) register_4 (.D(multiplexer_4_out), .Q(register_4_q), .clk(clock_1_out));  // open: en, clr
  Multiplexer #(.width(16)) multiplexer_5 (
    .in0(register_4_q), .in1(16'h2010), .out(multiplexer_5_out), .sel(in_1));  // open: en
  Register #(.width(16)) register_5 (.D(multiplexer_5_out), .Q(register_5_q), .clk(clock_1_out));  // open: en, clr
  Multiplexer #(.width(16)) multiplexer_6 (
    .in0(register_5_q), .in1(16'h1008), .out(multiplexer_6_out), .sel(in_1));  // open: en
  Register #(.width(16)) register_6 (.D(multiplexer_6_out), .Q(register_6_q), .clk(clock_1_out));  // open: en, clr
  Multiplexer #(.width(16)) multiplexer_7 (
    .in0(register_6_q), .in1(16'h804), .out(multiplexer_7_out), .sel(in_1));  // open: en
  Register #(.width(16)) register_7 (.D(multiplexer_7_out), .Q(register_7_q), .clk(clock_1_out));  // open: en, clr
  Register #(.width(16)) register_8 (.D(multiplexer_8_out), .Q(register_8_q), .clk(clock_1_out));  // open: en, clr
  Multiplexer #(.width(16)) multiplexer_8 (
    .in0(register_7_q), .in1(16'h402), .out(multiplexer_8_out), .sel(in_1));  // open: en
  DotMatrix #(.matrixcols(16), .matrixrows(16)) dotmatrix_1 (
    .col0(register_1_q), .col1(register_2_q), .col2(register_3_q), .col3(register_4_q), .col4(register_5_q),
    .col5(register_6_q), .col6(register_7_q), .col7(register_8_q), .col8(register_8_q), .col9(register_7_q),
    .col10(register_6_q), .col11(register_5_q), .col12(register_4_q), .col13(register_3_q),
    .col14(register_2_q), .col15(register_1_q));
endmodule
