// Logisim project mips_lw.circ as structural Verilog: 1 circuit, main circuit main
module main (
  input  [2:0] ALU_Ctrl,
  input  WE
);

  wire button_1_out, CLK_out;
  wire [7:0] adder_1_out, register_1_q;
  wire [31:0] bit_extender_1_out, main_1_rd1, main_2_y, ram_1_data, rom_1_data;

  Clock CLK (.out(CLK_out));
  Button button_1 (.out(button_1_out));
  Register register_1 (.D(adder_1_out), .Q(register_1_q), .clk(CLK_out), .clr(button_1_out));  // open: en
  Adder adder_1 (.a(register_1_q), .b(8'h4), .out(adder_1_out));  // open: cin, cout
  ROM #(.addrWidth(6), .dataWidth(32)) rom_1 (.addr(register_1_q[7:2]), .data(rom_1_data));  // open: sel
  // Probe on rom_1_data[31:26]
  assign bit_extender_1_out = {{16{rom_1_data[15]}}, rom_1_data[15:0]};  // Bit_Extender bit_extender_1
  RegFile_main main_1 (
    .A1(rom_1_data[25:21]), .in_3(CLK_out), .A3(rom_1_data[20:16]), .WD3(ram_1_data), .in_6(WE),
    .RD1(main_1_rd1));  // open: A2, RD2
  alu32_main main_2 (.A(main_1_rd1), .B(bit_extender_1_out), .F(ALU_Ctrl), .Y(main_2_y));  // open: Zero
  RAM #(.addrWidth(7), .dataWidth(32)) ram_1 (.addr(main_2_y[8:2]), .data(ram_1_data));  // open: sel, clk, ld, clr

  // Notes on the sheet:
  //   학번:35814, 성명: 이정근
  //   한림대학교 소프트웨어 융합 대학
  //   lw  $t2,  32($0)
  //   contents of rom_1 (hex, n*v repeats v):
  //   8c0a0020 8c0a0020 14b4820
  //   F = 010 --> ADD
endmodule
