// Logisim project mips_processor.circ as structural Verilog: 1 circuit, main circuit main
module main (
);

  wire AluSrc, and_1_out, Branch, button_1_out, CLK_out, Jump, main_2_zero, MemtoReg, MemWrite, RegDst,
       RegWrite;
  wire [2:0] ALUControl;
  wire [4:0] multiplexer_3_out;
  wire [5:0] Func, Opcode;
  wire [7:0] adder_1_out, multiplexer_1_out, multiplexer_2_out, PC_q, shifter_1_out;
  wire [19:0] rom_1_data, shifter_1_out_2;
  wire [27:0] bit_extender_2_out;
  wire [31:0] adder_2_out, bit_extender_1_out, bit_extender_3_out, main_1_rd1, main_1_rd2, main_2_y,
       main_3_output, main_3_rd, multiplexer_4_out, multiplexer_5_out, shifter_2_out;

  Clock CLK (.out(CLK_out));
  Multiplexer #(.width(8)) multiplexer_1 (
    .in0(adder_1_out), .in1(adder_2_out[7:0]), .out(multiplexer_1_out), .sel(and_1_out));  // open: en
  Multiplexer #(.width(8)) multiplexer_2 (
    .in0(multiplexer_1_out), .in1(shifter_1_out), .out(multiplexer_2_out), .sel(Jump));  // open: en
  Register PC (.D(multiplexer_2_out), .Q(PC_q), .clk(CLK_out), .clr(button_1_out));  // open: en
  Button button_1 (.out(button_1_out));
  Adder adder_1 (.a(PC_q), .b(8'h4), .out(adder_1_out));  // open: cin, cout
  // Probe on Opcode
  assign bit_extender_1_out = {{24{1'b0}}, adder_1_out};  // Bit_Extender bit_extender_1
  ROM #(.addrWidth(6), .dataWidth(32)) rom_1 (.addr(PC_q[7:2]), .data({Opcode, rom_1_data, Func}));  // open: sel
  Multiplexer #(.width(5)) multiplexer_3 (
    .in0(rom_1_data[14:10]), .in1(rom_1_data[9:5]), .out(multiplexer_3_out), .sel(RegDst));  // open: en
  assign bit_extender_2_out = {{2{1'b0}}, {rom_1_data, Func}};  // Bit_Extender bit_extender_2
  // Probe on multiplexer_3_out
  assign bit_extender_3_out = {{16{rom_1_data[9]}}, {rom_1_data[9:0], Func}};  // Bit_Extender bit_extender_3
  Shifter #(.width(28)) shifter_1 (.in(bit_extender_2_out), .\dist (5'b00010), .out({shifter_1_out_2, shifter_1_out}));
  RegFile_main main_1 (
    .A1(rom_1_data[19:15]), .A2(rom_1_data[14:10]), .in_3(CLK_out), .A3(multiplexer_3_out),
    .WD3(multiplexer_5_out), .in_6(RegWrite), .RD1(main_1_rd1), .RD2(main_1_rd2));
  Multiplexer #(.width(32)) multiplexer_4 (
    .in0(main_1_rd2), .in1(bit_extender_3_out), .out(multiplexer_4_out), .sel(AluSrc));  // open: en
  Shifter #(.width(32)) shifter_2 (.in(bit_extender_3_out), .\dist (5'b00010), .out(shifter_2_out));
  alu32_main main_2 (.A(main_1_rd1), .B(multiplexer_4_out), .F(ALUControl), .Y(main_2_y), .Zero(main_2_zero));
  Adder #(.width(32)) adder_2 (.a(shifter_2_out), .b(bit_extender_1_out), .out(adder_2_out));  // open: cin, cout
  and and_1 (and_1_out, Branch, main_2_zero);
  datamem_main main_3 (
    .A(main_2_y[8:0]), .CLK(CLK_out), .MemWrite(MemWrite), .WD(main_1_rd2), .RD(main_3_rd),
    .\output (main_3_output));
  Multiplexer #(.width(32)) multiplexer_5 (
    .in0(main_2_y), .in1(main_3_rd), .out(multiplexer_5_out), .sel(MemtoReg));  // open: en
  main_control_main main_4 (
    .opcode(Opcode), .Func(Func), .RegWrite(RegWrite), .RegDst(RegDst), .AluSrc(AluSrc), .Branch(Branch),
    .MemWrite(MemWrite), .MemtoReg(MemtoReg), .Jump(Jump), .ALUControl(ALUControl));
  _7_Segment_Display u_7_segment_display_1 (
    .g(main_3_output[6]), .f(main_3_output[7]), .a(main_3_output[0]), .b(main_3_output[1]),
    .e(main_3_output[5]), .d(main_3_output[4]), .c(main_3_output[3]), .dp(main_3_output[2]));
  _7_Segment_Display u_7_segment_display_2 (
    .g(main_3_output[14]), .f(main_3_output[15]), .a(main_3_output[8]), .b(main_3_output[9]),
    .e(main_3_output[13]), .d(main_3_output[12]), .c(main_3_output[11]), .dp(main_3_output[10]));

  // Notes on the sheet:
  //   한림대학교 소프트웨어 융합 대학
  //   학번:35814, 성명: 이정근
  //   lw  $t2,  32($0)
  //   014b4820 --> add $t1, $t2, $t3
  //   112a0004 --> beq $t1, $t2, 0x4
  //   contents of rom_1 (hex, n*v repeats v):
  //   20010abb ac010000 2001730a ac010000 20015b73 ac010000 2001ca5b ac010000 2001d9ca ac010000 2001f9d9
  //   ac010000 20010bf9 ac010000 2001fb0b ac010000 2001dbfb ac010000 2001bbdb ac010000 8000000
  //   F = 010 --> ADD
  //   Memory Mapped IO
endmodule
